# Fritzing sketch button_matrix (saved by Fritzing 1.0.2b)
breadboards: 1

parts:
  PICO = Raspberry Pi Pico W
  MATRIX = IC, SIP package, 5 pins [chip_label="Button Matrix"]

nets:
  N1: PICO.pin_1, MATRIX.pin4
  N2: PICO.pin_2, MATRIX.pin5
  N3: PICO.pin_5, MATRIX.pin2
  N4: PICO.pin_10, MATRIX.pin3
  N5: PICO.pin_36, MATRIX.pin1

custom parts:
  Raspberry Pi Pico W: Raspberry Pi Pico W. Based around the RP2040 microcontroller the Pico W is a low cost microcontroller device bringing Raspberry Pi quality, cost, and easy of use to the microcontroller space. The areas marked KEEPOUT in pcb silkscreen should not have traces running through them to avoid shorts on a soldered in module!
