# Fritzing sketch buttons (saved by Fritzing 1.0.2b)
breadboards: 1

parts:
  PICO = Raspberry Pi Pico W
  OK = Pushbutton [package="[THT]"]
  DOWN = Pushbutton [package="[THT]"]
  UP = Pushbutton [package="[THT]"]
  BACK = Pushbutton [package="[THT]"]

nets:
  N1: PICO.pin_1, UP.Pin_1, UP.Pin_2
  N2: PICO.pin_2, OK.Pin_1, OK.Pin_2
  N3: PICO.pin_5, DOWN.Pin_1, DOWN.Pin_2
  N4: PICO.pin_10, BACK.Pin_1, BACK.Pin_2
  N5: PICO.pin_36, OK.Pin_3, OK.Pin_4, DOWN.Pin_3, DOWN.Pin_4, UP.Pin_4, BACK.Pin_3, BACK.Pin_4

custom parts:
  Raspberry Pi Pico W: Raspberry Pi Pico W. Based around the RP2040 microcontroller the Pico W is a low cost microcontroller device bringing Raspberry Pi quality, cost, and easy of use to the microcontroller space. The areas marked KEEPOUT in pcb silkscreen should not have traces running through them to avoid shorts on a soldered in module!
