# Fritzing sketch display (saved by Fritzing 1.0.0d)

parts:
  Squix2 = OLED 0.96" 128x64 I2C SSD1306
  Mod2 = Raspberry Pi Pico

nets:
  N1: Squix2.VCC, Mod2.pin_36
  N2: Squix2.GND, Mod2.pin_3, Mod2.pin_38
  N3: Squix2.SCL, Mod2.pin_32
  N4: Squix2.SCA, Mod2.pin_31

notes:
  SCL ist das gleiche wie SCK
  achtung + und - könnten vertauscht sein

custom parts:
  Raspberry Pi Pico: Raspberry Pi Pico. Based around the RP2040 microcontroller the Pico is a low cost microcontroller device bringing Raspberry Pi quality, cost, and easy of use to the microcontroller space. Jan 2021, Split part in to two versions: tht (this one) and SMD. This one will drill holes for a .1 in header in pcb to allow plugging in the module as well as providing pads to solder the module to the top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
