# Fritzing sketch leds (saved by Fritzing 1.0.2b)
breadboards: 1

parts:
  PICO = Raspberry Pi Pico W
  part = LED - 5mm [color="Green (565nm)" current=0.030A package="5 mm [THT]"]
  part_2 = LED - 5mm [color="Yellow (592nm)" current=0.030A package="5 mm [THT]"]
  part_3 = LED - 5mm [color="Red (635nm)" current=0.030A package="5 mm [THT]"]
  R1 = Resistor [tolerance=±5% power=0.25W resistance=330 package=THT]
  R2 = Resistor [tolerance=±5% power=0.25W resistance=330 package=THT]
  R3 = Resistor [tolerance=±5% power=0.25W resistance=330 package=THT]

nets:
  N1: PICO.pin_3, PICO.pin_8, R1.Pin_0, R2.Pin_0, R3.Pin_0
  N2: PICO.pin_6, part_3.anode
  N3: PICO.pin_7, part_2.anode
  N4: PICO.pin_9, part.anode
  N5: part.cathode, R3.Pin_1
  N6: part_2.cathode, R2.Pin_1
  N7: part_3.cathode, R1.Pin_1

custom parts:
  Raspberry Pi Pico W: Raspberry Pi Pico W. Based around the RP2040 microcontroller the Pico W is a low cost microcontroller device bringing Raspberry Pi quality, cost, and easy of use to the microcontroller space. The areas marked KEEPOUT in pcb silkscreen should not have traces running through them to avoid shorts on a soldered in module!
