# Fritzing sketch temp (saved by Fritzing 1.0.0d)

parts:
  Mod2 = Raspberry Pi Pico
  DS2 = DS18B20 1-Wire Temperature Sensor [part_number=DS18B20]

nets:
  N1: Mod2.pin_4, DS2.DQ
  N2: Mod2.pin_18, DS2.GND
  N3: Mod2.pin_36, DS2.VDD

notes:
  DS1820 Temperatursensor

custom parts:
  Raspberry Pi Pico: Raspberry Pi Pico. Based around the RP2040 microcontroller the Pico is a low cost microcontroller device bringing Raspberry Pi quality, cost, and easy of use to the microcontroller space. Jan 2021, Split part in to two versions: tht (this one) and SMD. This one will drill holes for a .1 in header in pcb to allow plugging in the module as well as providing pads to solder the module to the top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
