# Fritzing sketch plugs (saved by Fritzing 1.0.2b)
breadboards: 1

parts:
  Pico = Raspberry Pi Pico W
  I2C-5pin = IC, SIP package, 5 pins [chip_label=SensorPlug]
  OneWire-3pin = IC, SIP package, 3 pins [chip_label=OneWirePlug]
  TDS = IC, DIP package, 6 pins [chip_label=TDS-PCB]
  pH = IC, SIP package, 3 pins [chip_label=pH-PCB]
  TDS_plug = IC, SIP package, 4 pins [chip_label=TDSPlug]

nets:
  N1: Pico.pin_3, Pico.pin_8, I2C-5pin.pin3, OneWire-3pin.pin1, TDS.pin1, pH.pin1
  N2: Pico.pin_4, OneWire-3pin.pin2
  N3: Pico.pin_11, I2C-5pin.pin2
  N4: Pico.pin_12, I2C-5pin.pin1
  N5: Pico.pin_14, TDS_plug.pin2
  N6: Pico.pin_32, pH.pin3
  N7: Pico.pin_34, TDS.pin3
  N8: Pico.pin_36, I2C-5pin.pin5, OneWire-3pin.pin3, TDS.pin2, pH.pin2, TDS_plug.pin1
  N9: Pico.pin_39, I2C-5pin.pin4
  N10: TDS.pin4, TDS_plug.pin4
  N11: TDS.pin5, TDS_plug.pin3

custom parts:
  Raspberry Pi Pico W: Raspberry Pi Pico W. Based around the RP2040 microcontroller the Pico W is a low cost microcontroller device bringing Raspberry Pi quality, cost, and easy of use to the microcontroller space. The areas marked KEEPOUT in pcb silkscreen should not have traces running through them to avoid shorts on a soldered in module!
