# Fritzing sketch power (saved by Fritzing 1.0.2b)

parts:
  PICO = Raspberry Pi Pico W
  BMS = IC, SIP package, 6 pins [chip_label=MH-CD42]
  18650 = 18650 battery holder [package=battery-18650-kit]
  USB-C_Breakout = IC, SIP package, 4 pins [chip_label=USB-C]
  MicroUSB-Plug = IC, SIP package, 4 pins [chip_label=MicroUSB]
  S1 = Toggle Switch [package=THT]

nets:
  N1: PICO.pin_8, BMS.pin2
  N2: PICO.pin_39, S1.L2
  N3: BMS.pin1, S1.COM
  N4: BMS.pin3, 18650.+
  N5: BMS.pin4, 18650.-
  N6: BMS.pin5, USB-C_Breakout.pin4
  N7: BMS.pin6, USB-C_Breakout.pin1
  N8: USB-C_Breakout.pin2, MicroUSB-Plug.pin3
  N9: USB-C_Breakout.pin3, MicroUSB-Plug.pin2

notes:
  MicroUSB in Pico stecken

custom parts:
  Raspberry Pi Pico W: Raspberry Pi Pico W. Based around the RP2040 microcontroller the Pico W is a low cost microcontroller device bringing Raspberry Pi quality, cost, and easy of use to the microcontroller space. The areas marked KEEPOUT in pcb silkscreen should not have traces running through them to avoid shorts on a soldered in module!
  18650 battery holder: 18650 Battery Holder identical to the dual battery version.
