# Fritzing sketch tds (saved by Fritzing 1.0.0d)

parts:
  A2 = tds-sensor-meter-v1.0_1
  Mod2 = Raspberry Pi Pico

nets:
  N1: A2.pin1, Mod2.pin_34
  N2: A2.pin2, Mod2.pin_36
  N3: A2.pin3, Mod2.pin_38

custom parts:
  : TDS Meter V1.0 Development Board Water Meter Filter Measuring Water Sensor Module.
  Raspberry Pi Pico: Raspberry Pi Pico. Based around the RP2040 microcontroller the Pico is a low cost microcontroller device bringing Raspberry Pi quality, cost, and easy of use to the microcontroller space. Jan 2021, Split part in to two versions: tht (this one) and SMD. This one will drill holes for a .1 in header in pcb to allow plugging in the module as well as providing pads to solder the module to the top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
